// Digital circuit ALU8bits.dig as structural Verilog
module ALU8bits (
  input  [7:0] AC,
  input  [7:0] N,
  input  [2:0] Opcode,
  output [7:0] AC_out,
  output [7:0] MQ_out
);

  wire [7:0] Div_out, Div_resto, NAnd_out, ShiftD_out, ShiftE_out, Soma_out, Sub_out, XOR_out;
  wire [15:0] Mult_out;

  soma8bits soma8bits_1 (.A(AC), .B(N), .Cin(1'b0), .Out(Soma_out));  // open: Cout
  subtrator8bits subtrator8bits_1 (.A(AC), .B(N), .Out(Sub_out));  // open: Cout
  multiplicador8bits multiplicador8bits_1 (.A(AC), .B(N), .Out(Mult_out));  // open: Cout
  divisor8bits divisor8bits_1 (.A(AC), .B(N), .MQ(Div_out), .A_out(Div_resto));
  shift_esquerda8bits shift_esquerda8bits_1 (.A(AC), .Out(ShiftE_out));
  shift_direita8bits shift_direita8bits_1 (.A(AC), .Out(ShiftD_out));
  assign NAnd_out = ~(AC & N);  // NAnd nand_1, 8 bits wide
  assign XOR_out = AC ^ N;  // XOr xor_1, 8 bits wide
  Multiplexer #(.Bits(8), .Selector_Bits(3)) multiplexer_1 (
    .sel(Opcode), .in_0(Soma_out), .in_1(Sub_out), .in_2(Mult_out[7:0]), .in_3(Div_out), .in_4(ShiftE_out),
    .in_5(ShiftD_out), .in_6(NAnd_out), .in_7(XOR_out), .out(AC_out));
  Multiplexer #(.Selector_Bits(3), .Bits(8)) multiplexer_2 (
    .sel(Opcode), .in_0({8{1'b0}}), .in_1({8{1'b0}}), .in_2(Mult_out[15:8]), .in_3(Div_resto),
    .in_4({8{1'b0}}), .in_5({8{1'b0}}), .in_6({8{1'b0}}), .in_7({8{1'b0}}), .out(MQ_out));

  // Other names for the same wires on the sheet: Multi_LSB[7:0] = Mult_out[7:0]; Multi_MSB[7:0] = Mult_out[15:8];
  //   Selector[2:0] = Opcode
endmodule
