// Digital circuit divisor8bits.dig as structural Verilog
module divisor8bits (
  input  [7:0] A,
  input  [7:0] B,
  output [7:0] MQ,
  output [7:0] A_out
);

  wire [7:0] etapa_divisao_1_r_out, etapa_divisao_2_r_out, etapa_divisao_3_r_out, etapa_divisao_4_r_out,
       etapa_divisao_5_r_out, etapa_divisao_6_r_out, etapa_divisao_7_r_out;

  etapa_divisao etapa_divisao_1 (.R_in(A), .N_sh({B[0], {7{1'b0}}}), .R_out(etapa_divisao_1_r_out), .Q_bit(MQ[7]));
  etapa_divisao etapa_divisao_2 (
    .R_in(etapa_divisao_1_r_out), .N_sh({B[1:0], {6{1'b0}}}), .R_out(etapa_divisao_2_r_out), .Q_bit(MQ[6]));
  etapa_divisao etapa_divisao_3 (
    .R_in(etapa_divisao_2_r_out), .N_sh({B[2:0], {5{1'b0}}}), .R_out(etapa_divisao_3_r_out), .Q_bit(MQ[5]));
  etapa_divisao etapa_divisao_4 (
    .R_in(etapa_divisao_3_r_out), .N_sh({B[3:0], 4'b0000}), .R_out(etapa_divisao_4_r_out), .Q_bit(MQ[4]));
  etapa_divisao etapa_divisao_5 (
    .R_in(etapa_divisao_4_r_out), .N_sh({B[4:0], 3'b000}), .R_out(etapa_divisao_5_r_out), .Q_bit(MQ[3]));
  etapa_divisao etapa_divisao_6 (
    .R_in(etapa_divisao_5_r_out), .N_sh({B[5:0], 2'b00}), .R_out(etapa_divisao_6_r_out), .Q_bit(MQ[2]));
  etapa_divisao etapa_divisao_7 (
    .R_in(etapa_divisao_6_r_out), .N_sh({B[6:0], 1'b0}), .R_out(etapa_divisao_7_r_out), .Q_bit(MQ[1]));
  etapa_divisao etapa_divisao_8 (.R_in(etapa_divisao_7_r_out), .N_sh(B), .R_out(A_out), .Q_bit(MQ[0]));

  // Other names for the same wires on the sheet: B_shift_0[7:0] = B; B_shift_1[7:1] = B[6:0]; B_shift_2[7:2] = B[5:0];
  //   B_shift_3[7:3] = B[4:0]; B_shift_4[7:4] = B[3:0]; B_shift_5[7:5] = B[2:0]; B_shift_6[7:6] = B[1:0];
  //   B_shift_7[7] = B[0]; Q0 = MQ[0]; Q1 = MQ[1]; Q2 = MQ[2]; Q3 = MQ[3]; Q4 = MQ[4]; Q5 = MQ[5]; Q6 = MQ[6];
  //   Q7 = MQ[7]
endmodule
