// Digital circuit etapa_divisao.dig as structural Verilog
module etapa_divisao (
  input  [7:0] R_in,
  input  [7:0] N_sh,
  output [7:0] R_out,
  output Q_bit
);

  wire [7:0] subtrator8bits_1_out;

  subtrator8bits subtrator8bits_1 (.A(R_in), .B(N_sh), .Out(subtrator8bits_1_out), .Cout(Q_bit));
  Multiplexer #(.Bits(8)) multiplexer_1 (.sel(Q_bit), .in_0(R_in), .in_1(subtrator8bits_1_out), .out(R_out));
endmodule
