// Digital circuit multiplicador8bits.dig as structural Verilog
module multiplicador8bits (
  input  [7:0] A,
  input  [7:0] B,
  output [15:0] Out,
  output Cout
);

  wire soma8bits_2_cout, soma8bits_4_cout, soma8bits_6_cout, soma8bits_8_cout, soma8bits_10_cout,
       soma8bits_12_cout, soma8bits_14_cout;
  wire [7:0] PP0, PP1, PP2, PP3, PP4, PP5, PP6, PP7, S1, S1_plus, S2, S2_plus, S3, S3_plus, S4, S4_plus, S5,
       S5_plus, S6, S6_plus;

  produto_parcial produto_parcial_1 (.A(A), .ni(B[0]), .PP(PP0));
  produto_parcial produto_parcial_2 (.A(A), .ni(B[1]), .PP(PP1));
  produto_parcial produto_parcial_3 (.A(A), .ni(B[2]), .PP(PP2));
  produto_parcial produto_parcial_4 (.A(A), .ni(B[3]), .PP(PP3));
  produto_parcial produto_parcial_5 (.A(A), .ni(B[4]), .PP(PP4));
  produto_parcial produto_parcial_6 (.A(A), .ni(B[5]), .PP(PP5));
  produto_parcial produto_parcial_7 (.A(A), .ni(B[6]), .PP(PP6));
  produto_parcial produto_parcial_8 (.A(A), .ni(B[7]), .PP(PP7));
  soma8bits soma8bits_1 (.A({8{1'b0}}), .B({{7{1'b0}}, PP1[7]}), .Cin(soma8bits_2_cout), .Out(S1_plus));  // open: Cout
  soma8bits soma8bits_2 (.A(PP0), .B({PP1[6:0], 1'b0}), .Cin(1'b0), .Out(S1), .Cout(soma8bits_2_cout));
  soma8bits soma8bits_3 (.A(S1_plus), .B({{6{1'b0}}, PP2[7:6]}), .Cin(soma8bits_4_cout), .Out(S2_plus));  // open: Cout
  soma8bits soma8bits_4 (.A(S1), .B({PP2[5:0], 2'b00}), .Cin(1'b0), .Out(S2), .Cout(soma8bits_4_cout));
  soma8bits soma8bits_5 (.A(S2_plus), .B({{5{1'b0}}, PP3[7:5]}), .Cin(soma8bits_6_cout), .Out(S3_plus));  // open: Cout
  soma8bits soma8bits_6 (.A(S2), .B({PP3[4:0], 3'b000}), .Cin(1'b0), .Out(S3), .Cout(soma8bits_6_cout));
  soma8bits soma8bits_7 (.A(S3_plus), .B({4'b0000, PP4[7:4]}), .Cin(soma8bits_8_cout), .Out(S4_plus));  // open: Cout
  soma8bits soma8bits_8 (.A(S3), .B({PP4[3:0], 4'b0000}), .Cin(1'b0), .Out(S4), .Cout(soma8bits_8_cout));
  soma8bits soma8bits_9 (.A(S4_plus), .B({3'b000, PP5[7:3]}), .Cin(soma8bits_10_cout), .Out(S5_plus));  // open: Cout
  soma8bits soma8bits_10 (.A(S4), .B({PP5[2:0], {5{1'b0}}}), .Cin(1'b0), .Out(S5), .Cout(soma8bits_10_cout));
  soma8bits soma8bits_11 (.A(S5_plus), .B({2'b00, PP6[7:2]}), .Cin(soma8bits_12_cout), .Out(S6_plus));  // open: Cout
  soma8bits soma8bits_12 (.A(S5), .B({PP6[1:0], {6{1'b0}}}), .Cin(1'b0), .Out(S6), .Cout(soma8bits_12_cout));
  soma8bits soma8bits_13 (.A(S6_plus), .B({1'b0, PP7[7:1]}), .Cin(soma8bits_14_cout), .Out(Out[15:8]), .Cout(Cout));
  soma8bits soma8bits_14 (.A(S6), .B({PP7[0], {7{1'b0}}}), .Cin(1'b0), .Out(Out[7:0]), .Cout(soma8bits_14_cout));

  // Other names for the same wires on the sheet: PP0_0 = PP0[0]; PP0_1 = PP0[1]; PP0_2 = PP0[2]; PP0_3 = PP0[3];
  //   PP0_4 = PP0[4]; PP0_5 = PP0[5]; PP0_6 = PP0[6]; PP0_7 = PP0[7]; PP1_0 = PP1[0]; PP1_shift[7:1] = PP1[6:0];
  //   PP1_1 = PP1[1]; PP1_2 = PP1[2]; PP1_3 = PP1[3]; PP1_4 = PP1[4]; PP1_5 = PP1[5]; PP1_6 = PP1[6]; PP1_7 = PP1[7];
  //   PP2_0 = PP2[0]; PP2_shift[7:2] = PP2[5:0]; PP2_1 = PP2[1]; PP2_2 = PP2[2]; PP2_3 = PP2[3]; PP2_4 = PP2[4];
  //   PP2_5 = PP2[5]; PP2_6 = PP2[6]; PP2_7 = PP2[7]; PP3_0 = PP3[0]; PP3_shift[7:3] = PP3[4:0]; PP3_1 = PP3[1];
  //   PP3_2 = PP3[2]; PP3_3 = PP3[3]; PP3_4 = PP3[4]; PP3_5 = PP3[5]; PP3_6 = PP3[6]; PP3_7 = PP3[7]; PP4_0 = PP4[0];
  //   PP4_shift[7:4] = PP4[3:0]; PP4_1 = PP4[1]; PP4_2 = PP4[2]; PP4_3 = PP4[3]; PP4_4 = PP4[4]; PP4_5 = PP4[5];
  //   PP4_6 = PP4[6]; PP4_7 = PP4[7]; PP5_0 = PP5[0]; PP5_shift[7:5] = PP5[2:0]; PP5_1 = PP5[1]; PP5_2 = PP5[2];
  //   PP5_3 = PP5[3]; PP5_4 = PP5[4]; PP5_5 = PP5[5]; PP5_6 = PP5[6]; PP5_7 = PP5[7]; PP6_0 = PP6[0];
  //   PP6_shift[7:6] = PP6[1:0]; PP6_1 = PP6[1]; PP6_2 = PP6[2]; PP6_3 = PP6[3]; PP6_4 = PP6[4]; PP6_5 = PP6[5];
  //   PP6_6 = PP6[6]; PP6_7 = PP6[7]; PP7_0 = PP7[0]; PP7_shift[7] = PP7[0]; PP7_1 = PP7[1]; PP7_2 = PP7[2];
  //   PP7_3 = PP7[3]; PP7_4 = PP7[4]; PP7_5 = PP7[5]; PP7_6 = PP7[6]; PP7_7 = PP7[7]; S7[7:0] = Out[7:0];
  //   S7_plus[7:0] = Out[15:8]
endmodule
