// Digital circuit produto_parcial.dig as structural Verilog
module produto_parcial (
  input  [7:0] A,
  input  ni,
  output [7:0] PP
);

  and and_1 (PP[0], A[0], ni);
  and and_2 (PP[1], A[1], ni);
  and and_3 (PP[2], A[2], ni);
  and and_4 (PP[3], A[3], ni);
  and and_5 (PP[4], A[4], ni);
  and and_6 (PP[5], A[5], ni);
  and and_7 (PP[6], A[6], ni);
  and and_8 (PP[7], A[7], ni);
endmodule
