// Digital circuit soma8bits.dig as structural Verilog
module soma8bits (
  input  [7:0] A,
  input  [7:0] B,
  input  Cin,
  output [7:0] Out,
  output Cout
);

  wire soma1bit_1_cout, soma1bit_2_cout, soma1bit_3_cout, soma1bit_4_cout, soma1bit_5_cout, soma1bit_6_cout,
       soma1bit_7_cout;

  soma1bit soma1bit_1 (.A(A[0]), .B(B[0]), .Cin(Cin), .S(Out[0]), .Cout(soma1bit_1_cout));
  soma1bit soma1bit_2 (.A(A[1]), .B(B[1]), .Cin(soma1bit_1_cout), .S(Out[1]), .Cout(soma1bit_2_cout));
  soma1bit soma1bit_3 (.A(A[2]), .B(B[2]), .Cin(soma1bit_2_cout), .S(Out[2]), .Cout(soma1bit_3_cout));
  soma1bit soma1bit_4 (.A(A[3]), .B(B[3]), .Cin(soma1bit_3_cout), .S(Out[3]), .Cout(soma1bit_4_cout));
  soma1bit soma1bit_5 (.A(A[4]), .B(B[4]), .Cin(soma1bit_4_cout), .S(Out[4]), .Cout(soma1bit_5_cout));
  soma1bit soma1bit_6 (.A(A[5]), .B(B[5]), .Cin(soma1bit_5_cout), .S(Out[5]), .Cout(soma1bit_6_cout));
  soma1bit soma1bit_7 (.A(A[6]), .B(B[6]), .Cin(soma1bit_6_cout), .S(Out[6]), .Cout(soma1bit_7_cout));
  soma1bit soma1bit_8 (.A(A[7]), .B(B[7]), .Cin(soma1bit_7_cout), .S(Out[7]), .Cout(Cout));

  // Other names for the same wires on the sheet: S0 = Out[0]; S1 = Out[1]; S2 = Out[2]; S3 = Out[3]; S4 = Out[4];
  //   S5 = Out[5]; S6 = Out[6]; S7 = Out[7]
endmodule
