// Digital circuit subtrator8bits.dig as structural Verilog
module subtrator8bits (
  input  [7:0] A,
  input  [7:0] B,
  output [7:0] Out,
  output Cout
);

  wire [7:0] inversor_comp_1_ainv, inversor_comp_2_ainv, soma8bits_1_out;

  inversor_comp inversor_comp_1 (.A(B), .Ainv(inversor_comp_1_ainv));
  soma8bits soma8bits_1 (.A(A), .B(inversor_comp_1_ainv), .Cin(1'b0), .Out(soma8bits_1_out), .Cout(Cout));
  inversor_comp inversor_comp_2 (.A(soma8bits_1_out), .Ainv(inversor_comp_2_ainv));
  Multiplexer #(.Bits(8)) multiplexer_1 (
    .sel(soma8bits_1_out[7]), .in_0(soma8bits_1_out), .in_1(inversor_comp_2_ainv), .out(Out));
  LED plus (.in(soma8bits_1_out[7]));
endmodule
